// Logisim project lab1-2二进制全加器.circ as structural Verilog: 2 circuits, main circuit main
module main (
  input  A,
  input  B,
  input  Ci,
  output S,
  output C
);

  wire and_1_out, and_2_out, xor_1_out;

  and and_1 (and_1_out, A, B);
  xor xor_1 (xor_1_out, A, B);
  xor xor_2 (S, A, B, Ci);
  and and_2 (and_2_out, xor_1_out, Ci);
  or or_1 (C, and_1_out, and_2_out);
endmodule

module test (
  input  in_1,
  input  in_2,
  input  in_3,
  output out_4,
  output out_5
);

  main main_1 (.A(in_1), .B(in_2), .Ci(in_3), .S(out_4), .C(out_5));
endmodule
