// Logisim project 实验1-cs1806-U201814788-刘美.circ as structural Verilog: 5 circuits, main circuit lab1-1一位二进制半加器
module \lab1_1一位二进制半加器  (
  input  A,
  input  B,
  output S,
  output out_4
);

  xor xor_1 (S, A, B);
  and and_1 (out_4, A, B);
endmodule

module \lb1_2一位二进制全加器  (
  input  A,
  input  B,
  input  Ci,
  output S,
  output C
);

  wire and_1_out, and_2_out, xor_1_out;

  and and_1 (and_1_out, A, B);
  xor xor_1 (xor_1_out, A, B);
  xor xor_2 (S, A, B, Ci);
  and and_2 (and_2_out, xor_1_out, Ci);
  or or_1 (C, and_1_out, and_2_out);
endmodule

module \lab1_3串行进位四位二进制全加器  (
  input  C0,
  input  A0,
  input  A1,
  input  A2,
  input  A3,
  input  B0,
  input  B1,
  input  B2,
  input  B3,
  output S0,
  output S1,
  output S2,
  output S3,
  output C4
);

  wire \lb1_2一位二进制全加器_1_c , \lb1_2一位二进制全加器_2_c , \lb1_2一位二进制全加器_3_c ;

  \lb1_2一位二进制全加器  \lb1_2一位二进制全加器_1  (.A(A0), .B(B0), .Ci(C0), .S(S0), .C(\lb1_2一位二进制全加器_1_c ));
  \lb1_2一位二进制全加器  \lb1_2一位二进制全加器_2  (.A(A1), .B(B1), .Ci(\lb1_2一位二进制全加器_1_c ), .S(S1), .C(\lb1_2一位二进制全加器_2_c ));
  \lb1_2一位二进制全加器  \lb1_2一位二进制全加器_3  (.A(A2), .B(B2), .Ci(\lb1_2一位二进制全加器_2_c ), .S(S2), .C(\lb1_2一位二进制全加器_3_c ));
  \lb1_2一位二进制全加器  \lb1_2一位二进制全加器_4  (.A(A3), .B(B3), .Ci(\lb1_2一位二进制全加器_3_c ), .S(S3), .C(C4));
endmodule

module \lab1_4先行进位四位二进制并行全加器  (
  input  C0,
  input  A0,
  input  B0,
  input  A1,
  input  B1,
  input  A2,
  input  B2,
  input  A3,
  input  B3,
  output S2,
  output S3,
  output C4,
  output S0,
  output S1
);

  wire and_1_out, and_2_out, and_3_out, and_4_out, and_5_out, and_6_out, and_7_out, and_8_out, and_9_out,
       and_10_out, and_11_out, and_12_out, and_13_out, and_14_out, or_1_out, or_2_out, or_3_out, xor_2_out,
       xor_4_out, xor_6_out, xor_8_out;

  xor xor_1 (S0, C0, xor_2_out);
  xor xor_2 (xor_2_out, A0, B0);
  or or_1 (or_1_out, and_1_out, and_2_out);
  and and_1 (and_1_out, C0, xor_2_out);
  xor xor_3 (S1, or_1_out, xor_4_out);
  and and_2 (and_2_out, B0, A0);
  xor xor_4 (xor_4_out, A1, B1);
  and and_3 (and_3_out, and_2_out, xor_4_out);
  and and_4 (and_4_out, C0, xor_2_out, xor_4_out);
  xor xor_5 (S2, or_2_out, xor_6_out);
  or or_2 (or_2_out, and_4_out, and_3_out, and_5_out);
  and and_5 (and_5_out, B1, A1);
  or or_3 (or_3_out, and_6_out, and_7_out, and_8_out, and_9_out);
  and and_6 (and_6_out, C0, xor_2_out, xor_4_out, xor_6_out);
  xor xor_6 (xor_6_out, A2, B2);
  xor xor_7 (S3, or_3_out, xor_8_out);
  and and_7 (and_7_out, and_2_out, xor_4_out, xor_6_out);
  and and_8 (and_8_out, and_5_out, xor_6_out);
  and and_9 (and_9_out, B2, A2);
  and and_10 (and_10_out, C0, xor_2_out, xor_4_out, xor_6_out, xor_8_out);
  and and_11 (and_11_out, and_2_out, xor_4_out, xor_6_out, xor_8_out);
  xor xor_8 (xor_8_out, A3, B3);
  or or_4 (C4, and_10_out, and_11_out, and_12_out, and_13_out, and_14_out);
  and and_12 (and_12_out, and_5_out, xor_6_out, xor_8_out);
  and and_13 (and_13_out, and_9_out, xor_8_out);
  and and_14 (and_14_out, B3, A3);
endmodule

module test (
  input  in_1,
  input  in_2,
  input  in_3,
  input  in_4,
  input  in_5,
  input  in_6,
  input  in_7,
  input  in_8,
  input  in_9,
  output out_10,
  output out_11,
  output out_12,
  output out_13,
  output out_14
);

  \lab1_4先行进位四位二进制并行全加器  \lab1_4先行进位四位二进制并行全加器_1  (
    .S0(out_13), .C0(in_1), .B0(in_9), .S1(out_12), .S2(out_11), .S3(out_10), .C4(out_14), .B1(in_8),
    .A2(in_3), .B2(in_7), .A3(in_2), .B3(in_6), .A0(in_5), .A1(in_4));
endmodule
