// Logisim project 实验3-CS1806-U201814788-刘美.circ as structural Verilog: 7 circuits, main circuit 四位乘法器
module \四位乘法器  (
  input  [3:0] a,
  input  [3:0] b,
  output [7:0] out_3
);

  wire [7:0] adder_1_out, adder_2_out, adder_3_out, adder_4_out, bit_extender_1_out, multiplexer_1_out,
       multiplexer_2_out, multiplexer_3_out, shifter_1_out, shifter_2_out, shifter_3_out;

  assign bit_extender_1_out = {{4{1'b0}}, b};  // Bit_Extender bit_extender_1
  Adder adder_1 (.a({8{1'b0}}), .b(bit_extender_1_out), .out(adder_1_out));  // open: cin, cout
  Shifter shifter_1 (.in(bit_extender_1_out), .\dist (3'b001), .out(shifter_1_out));
  Multiplexer #(.width(8), .enable("false")) multiplexer_1 (
    .in0({8{1'b0}}), .in1(adder_1_out), .out(multiplexer_1_out), .sel(a[0]));
  Adder adder_2 (.a(multiplexer_1_out), .b(shifter_1_out), .out(adder_2_out));  // open: cin, cout
  Shifter shifter_2 (.in(shifter_1_out), .\dist (3'b001), .out(shifter_2_out));
  Multiplexer #(.width(8), .enable("false")) multiplexer_2 (
    .in0(multiplexer_1_out), .in1(adder_2_out), .out(multiplexer_2_out), .sel(a[1]));
  Adder adder_3 (.a(multiplexer_2_out), .b(shifter_2_out), .out(adder_3_out));  // open: cin, cout
  Multiplexer #(.width(8), .enable("false")) multiplexer_3 (
    .in0(multiplexer_2_out), .in1(adder_3_out), .out(multiplexer_3_out), .sel(a[2]));
  Shifter shifter_3 (.in(shifter_2_out), .\dist (3'b001), .out(shifter_3_out));
  Adder adder_4 (.a(multiplexer_3_out), .b(shifter_3_out), .out(adder_4_out));  // open: cin, cout
  Multiplexer #(.width(8), .enable("false")) multiplexer_4 (
    .in0(multiplexer_3_out), .in1(adder_4_out), .out(out_3), .sel(a[3]));
endmodule

module \四位乘法器测试电路  (
  input  [3:0] in_1,
  input  [3:0] in_2,
  output [7:0] out_3
);

  \四位乘法器  \u_四位乘法器_1  (.a(in_1), .b(in_2), .out_3(out_3));
endmodule

module \_32X4乘法器  (
  input  [3:0] a,
  input  [31:0] b,
  output [31:0] out_3,
  output [31:0] out_4
);

  wire adder_3_cout, adder_5_cout, adder_6_cout;
  wire [31:0] adder_1_out, adder_2_out, adder_3_out, adder_4_out, adder_5_out, adder_6_out, adder_7_out,
       multiplexer_1_out, multiplexer_2_out, multiplexer_3_out, multiplexer_4_out, multiplexer_5_out,
       shifter_1_out, shifter_2_out, shifter_3_out, shifter_4_out, shifter_5_out, shifter_6_out;

  Adder #(.width(32)) adder_1 (.a({32{1'b0}}), .b(b), .out(adder_1_out));  // open: cin, cout
  Shifter #(.width(32)) shifter_1 (.in(b), .\dist (5'b00001), .out(shifter_1_out));
  Shifter #(.width(32), .shift("lr")) shifter_2 (.in(b), .\dist ({5{1'b1}}), .out(shifter_2_out));
  Multiplexer #(.width(32), .enable("false")) multiplexer_1 (
    .in0({32{1'b0}}), .in1(adder_1_out), .out(multiplexer_1_out), .sel(a[0]));
  Adder #(.width(32)) adder_2 (.a({32{1'b0}}), .b(shifter_2_out), .out(adder_2_out), .cin(adder_3_cout));  // open: cout
  Multiplexer #(.width(32), .enable("false")) multiplexer_2 (
    .in0({32{1'b0}}), .in1(adder_2_out), .out(multiplexer_2_out), .sel(a[1]));
  Adder #(.width(32)) adder_3 (
    .a(multiplexer_1_out), .b(shifter_1_out), .out(adder_3_out), .cout(adder_3_cout));  // open: cin
  Shifter #(.width(32)) shifter_3 (.in(shifter_1_out), .\dist (5'b00001), .out(shifter_3_out));
  Shifter #(.width(32), .shift("lr")) shifter_4 (.in(b), .\dist (5'b11110), .out(shifter_4_out));
  Multiplexer #(.width(32), .enable("false")) multiplexer_3 (
    .in0(multiplexer_1_out), .in1(adder_3_out), .out(multiplexer_3_out), .sel(a[1]));
  Adder #(.width(32)) adder_4 (
    .a(multiplexer_2_out), .b(shifter_4_out), .out(adder_4_out), .cin(adder_5_cout));  // open: cout
  Adder #(.width(32)) adder_5 (
    .a(multiplexer_3_out), .b(shifter_3_out), .out(adder_5_out), .cout(adder_5_cout));  // open: cin
  Multiplexer #(.width(32), .enable("false")) multiplexer_4 (
    .in0(multiplexer_2_out), .in1(adder_4_out), .out(multiplexer_4_out), .sel(a[2]));
  Multiplexer #(.width(32), .enable("false")) multiplexer_5 (
    .in0(multiplexer_3_out), .in1(adder_5_out), .out(multiplexer_5_out), .sel(a[2]));
  Shifter #(.width(32)) shifter_5 (.in(shifter_3_out), .\dist (5'b00001), .out(shifter_5_out));
  Shifter #(.width(32), .shift("lr")) shifter_6 (.in(b), .\dist (5'b11101), .out(shifter_6_out));
  Adder #(.width(32)) adder_6 (
    .a(multiplexer_5_out), .b(shifter_5_out), .out(adder_6_out), .cout(adder_6_cout));  // open: cin
  Adder #(.width(32)) adder_7 (
    .a(multiplexer_4_out), .b(shifter_6_out), .out(adder_7_out), .cin(adder_6_cout));  // open: cout
  Multiplexer #(.width(32), .enable("false")) multiplexer_6 (
    .in0(multiplexer_5_out), .in1(adder_6_out), .out(out_3), .sel(a[3]));
  Multiplexer #(.width(32), .enable("false")) multiplexer_7 (
    .in0(multiplexer_4_out), .in1(adder_7_out), .out(out_4), .sel(a[3]));
endmodule

module \_32X4乘法器测试电路  (
  input  [3:0] in_1,
  input  [31:0] in_2,
  input  [31:0] in_3,
  input  [31:0] in_4,
  output [31:0] out_5,
  output [31:0] out_6,
  output [31:0] out_7,
  output [31:0] out_8
);

  \_32X4乘法器  \u_32x4乘法器_1  (.a(in_1), .b(in_2), .out_3(out_5), .out_4(out_6));
  Multiplier #(.width(32)) multiplier_1 (.a(in_3), .b(in_4), .out(out_7), .cout(out_8));  // open: cin
endmodule

module \_32X32乘法器  (
  input  [31:0] a_31_0,
  input  [31:0] b_31_0,
  output [31:0] p_31_0,
  output [31:0] pc_31_0
);

  wire adder_1_cout, adder_2_cout, adder_3_cout, adder_4_cout, adder_5_cout, adder_6_cout, adder_7_cout;
  wire [31:0] adder_1_out, adder_2_out, adder_3_out, adder_5_out, adder_6_out, adder_7_out, adder_8_out,
       adder_9_out, adder_10_out, adder_11_out, adder_12_out, adder_13_out, adder_14_out, adder_16_out,
       adder_17_out, adder_18_out, adder_19_out, adder_20_out, adder_21_out, \n32x4乘法器_1_out_3 ,
       \n32x4乘法器_1_out_4 , \n32x4乘法器_2_out_3 , \n32x4乘法器_2_out_4 , \n32x4乘法器_3_out_3 , \n32x4乘法器_3_out_4 ,
       \n32x4乘法器_4_out_3 , \n32x4乘法器_4_out_4 , \n32x4乘法器_5_out_3 , \n32x4乘法器_5_out_4 , \n32x4乘法器_6_out_3 ,
       \n32x4乘法器_6_out_4 , \n32x4乘法器_7_out_3 , \n32x4乘法器_7_out_4 , \n32x4乘法器_8_out_3 , \n32x4乘法器_8_out_4 ,
       shifter_1_out, shifter_2_out, shifter_3_out, shifter_4_out, shifter_5_out, shifter_6_out,
       shifter_7_out, shifter_8_out, shifter_9_out, shifter_10_out, shifter_11_out, shifter_12_out,
       shifter_13_out, shifter_14_out, shifter_15_out, shifter_16_out, shifter_17_out, shifter_18_out,
       shifter_19_out, shifter_20_out, shifter_21_out;

  \_32X4乘法器  \u_32x4乘法器_1  (.a(a_31_0[31:28]), .b(b_31_0), .out_3(\n32x4乘法器_1_out_3 ), .out_4(\n32x4乘法器_1_out_4 ));
  \_32X4乘法器  \u_32x4乘法器_2  (.a(a_31_0[27:24]), .b(b_31_0), .out_3(\n32x4乘法器_2_out_3 ), .out_4(\n32x4乘法器_2_out_4 ));
  \_32X4乘法器  \u_32x4乘法器_3  (.a(a_31_0[23:20]), .b(b_31_0), .out_3(\n32x4乘法器_3_out_3 ), .out_4(\n32x4乘法器_3_out_4 ));
  \_32X4乘法器  \u_32x4乘法器_4  (.a(a_31_0[19:16]), .b(b_31_0), .out_3(\n32x4乘法器_4_out_3 ), .out_4(\n32x4乘法器_4_out_4 ));
  \_32X4乘法器  \u_32x4乘法器_5  (.a(a_31_0[15:12]), .b(b_31_0), .out_3(\n32x4乘法器_5_out_3 ), .out_4(\n32x4乘法器_5_out_4 ));
  \_32X4乘法器  \u_32x4乘法器_6  (.a(a_31_0[11:8]), .b(b_31_0), .out_3(\n32x4乘法器_6_out_3 ), .out_4(\n32x4乘法器_6_out_4 ));
  \_32X4乘法器  \u_32x4乘法器_7  (.a(a_31_0[7:4]), .b(b_31_0), .out_3(\n32x4乘法器_7_out_3 ), .out_4(\n32x4乘法器_7_out_4 ));
  \_32X4乘法器  \u_32x4乘法器_8  (.a(a_31_0[3:0]), .b(b_31_0), .out_3(\n32x4乘法器_8_out_3 ), .out_4(\n32x4乘法器_8_out_4 ));
  Shifter #(.width(32)) shifter_1 (.in(\n32x4乘法器_1_out_3 ), .\dist (5'b11100), .out(shifter_1_out));
  Shifter #(.width(32)) shifter_2 (.in(\n32x4乘法器_1_out_4 ), .\dist (5'b11100), .out(shifter_2_out));
  Shifter #(.width(32)) shifter_3 (.in(\n32x4乘法器_2_out_3 ), .\dist (5'b11000), .out(shifter_3_out));
  Shifter #(.width(32)) shifter_4 (.in(\n32x4乘法器_2_out_4 ), .\dist (5'b11000), .out(shifter_4_out));
  Shifter #(.width(32)) shifter_5 (.in(\n32x4乘法器_3_out_3 ), .\dist (5'b10100), .out(shifter_5_out));
  Shifter #(.width(32)) shifter_6 (.in(\n32x4乘法器_3_out_4 ), .\dist (5'b10100), .out(shifter_6_out));
  Shifter #(.width(32)) shifter_7 (.in(\n32x4乘法器_4_out_3 ), .\dist (5'b10000), .out(shifter_7_out));
  Shifter #(.width(32)) shifter_8 (.in(\n32x4乘法器_4_out_4 ), .\dist (5'b10000), .out(shifter_8_out));
  Shifter #(.width(32)) shifter_9 (.in(\n32x4乘法器_5_out_3 ), .\dist (5'b01100), .out(shifter_9_out));
  Shifter #(.width(32)) shifter_10 (.in(\n32x4乘法器_5_out_4 ), .\dist (5'b01100), .out(shifter_10_out));
  Shifter #(.width(32)) shifter_11 (.in(\n32x4乘法器_6_out_3 ), .\dist (5'b01000), .out(shifter_11_out));
  Shifter #(.width(32)) shifter_12 (.in(\n32x4乘法器_6_out_4 ), .\dist (5'b01000), .out(shifter_12_out));
  Shifter #(.width(32)) shifter_13 (.in(\n32x4乘法器_7_out_3 ), .\dist (5'b00100), .out(shifter_13_out));
  Shifter #(.width(32)) shifter_14 (.in(\n32x4乘法器_7_out_4 ), .\dist (5'b00100), .out(shifter_14_out));
  Shifter #(.width(32), .shift("lr")) shifter_15 (.in(\n32x4乘法器_1_out_3 ), .\dist (5'b00100), .out(shifter_15_out));
  Shifter #(.width(32), .shift("lr")) shifter_16 (.in(\n32x4乘法器_2_out_3 ), .\dist (5'b01000), .out(shifter_16_out));
  Shifter #(.width(32), .shift("lr")) shifter_17 (.in(\n32x4乘法器_3_out_3 ), .\dist (5'b01100), .out(shifter_17_out));
  Shifter #(.width(32), .shift("lr")) shifter_18 (.in(\n32x4乘法器_4_out_3 ), .\dist (5'b10000), .out(shifter_18_out));
  Adder #(.width(32)) adder_1 (
    .a(shifter_9_out), .b(adder_2_out), .out(adder_1_out), .cout(adder_1_cout));  // open: cin
  Shifter #(.width(32), .shift("lr")) shifter_19 (.in(\n32x4乘法器_5_out_3 ), .\dist (5'b10100), .out(shifter_19_out));
  Adder #(.width(32)) adder_2 (
    .a(adder_3_out), .b(shifter_11_out), .out(adder_2_out), .cout(adder_2_cout));  // open: cin
  Shifter #(.width(32), .shift("lr")) shifter_20 (.in(\n32x4乘法器_6_out_3 ), .\dist (5'b11000), .out(shifter_20_out));
  Adder #(.width(32)) adder_3 (
    .a(shifter_13_out), .b(\n32x4乘法器_8_out_3 ), .out(adder_3_out), .cout(adder_3_cout));  // open: cin
  Adder #(.width(32)) adder_4 (.a(shifter_1_out), .b(adder_5_out), .out(p_31_0), .cout(adder_4_cout));  // open: cin
  Adder #(.width(32)) adder_5 (
    .a(shifter_3_out), .b(adder_6_out), .out(adder_5_out), .cout(adder_5_cout));  // open: cin
  Adder #(.width(32)) adder_6 (
    .a(shifter_5_out), .b(adder_7_out), .out(adder_6_out), .cout(adder_6_cout));  // open: cin
  Adder #(.width(32)) adder_7 (
    .a(shifter_7_out), .b(adder_1_out), .out(adder_7_out), .cout(adder_7_cout));  // open: cin
  Shifter #(.width(32), .shift("lr")) shifter_21 (.in(\n32x4乘法器_7_out_3 ), .\dist (5'b11100), .out(shifter_21_out));
  Adder #(.width(32)) adder_8 (.a(shifter_15_out), .b(shifter_2_out), .out(adder_8_out));  // open: cin, cout
  Adder #(.width(32)) adder_9 (.a(shifter_16_out), .b(shifter_4_out), .out(adder_9_out));  // open: cin, cout
  Adder #(.width(32)) adder_10 (.a(shifter_17_out), .b(shifter_6_out), .out(adder_10_out));  // open: cin, cout
  Adder #(.width(32)) adder_11 (.a(shifter_18_out), .b(shifter_8_out), .out(adder_11_out));  // open: cin, cout
  Adder #(.width(32)) adder_12 (.a(shifter_19_out), .b(shifter_10_out), .out(adder_12_out));  // open: cin, cout
  Adder #(.width(32)) adder_13 (.a(shifter_20_out), .b(shifter_12_out), .out(adder_13_out));  // open: cin, cout
  Adder #(.width(32)) adder_14 (.a(shifter_14_out), .b(shifter_21_out), .out(adder_14_out));  // open: cin, cout
  Adder #(.width(32)) adder_15 (.a(adder_8_out), .b(adder_16_out), .out(pc_31_0), .cin(adder_4_cout));  // open: cout
  Adder #(.width(32)) adder_16 (
    .a(adder_9_out), .b(adder_17_out), .out(adder_16_out), .cin(adder_5_cout));  // open: cout
  Adder #(.width(32)) adder_17 (
    .a(adder_10_out), .b(adder_18_out), .out(adder_17_out), .cin(adder_6_cout));  // open: cout
  Adder #(.width(32)) adder_18 (
    .a(adder_11_out), .b(adder_19_out), .out(adder_18_out), .cin(adder_7_cout));  // open: cout
  Adder #(.width(32)) adder_19 (
    .a(adder_12_out), .b(adder_20_out), .out(adder_19_out), .cin(adder_1_cout));  // open: cout
  Adder #(.width(32)) adder_20 (
    .a(adder_13_out), .b(adder_21_out), .out(adder_20_out), .cin(adder_2_cout));  // open: cout
  Adder #(.width(32)) adder_21 (
    .a(adder_14_out), .b(\n32x4乘法器_8_out_4 ), .out(adder_21_out), .cin(adder_3_cout));  // open: cout
endmodule

module \_32X32乘法器测试电路  (
  input  [31:0] in_1,
  input  [31:0] in_2,
  input  [31:0] in_3,
  input  [31:0] in_4,
  output [31:0] out_5,
  output [31:0] out_6,
  output [31:0] out_7,
  output [31:0] out_8
);

  Multiplier #(.width(32)) multiplier_1 (.a(in_3), .b(in_4), .out(out_7), .cout(out_8));  // open: cin
  \_32X32乘法器  \u_32x32乘法器_1  (.b_31_0(in_1), .p_31_0(out_5), .pc_31_0(out_6), .a_31_0(in_2));
endmodule

module test (
  input  [31:0] a_31_0,
  input  [31:0] b_31_0,
  output [31:0] p_31_0,
  output [31:0] pc_31_0
);

  wire adder_1_cout, adder_2_cout, adder_3_cout, adder_4_cout, adder_5_cout, adder_6_cout, adder_7_cout,
       adder_8_cout, adder_9_cout, adder_10_cout, adder_11_cout, adder_12_cout, adder_13_cout;
  wire [31:0] adder_1_out, adder_2_out, adder_3_out, adder_4_out, adder_5_out, adder_6_out, adder_8_out,
       adder_9_out, adder_10_out, adder_11_out, adder_12_out, adder_13_out, \n32x4乘法器_1_out_3 ,
       \n32x4乘法器_1_out_4 , \n32x4乘法器_2_out_3 , \n32x4乘法器_2_out_4 , \n32x4乘法器_3_out_3 , \n32x4乘法器_3_out_4 ,
       \n32x4乘法器_4_out_3 , \n32x4乘法器_4_out_4 , \n32x4乘法器_5_out_3 , \n32x4乘法器_5_out_4 , \n32x4乘法器_6_out_3 ,
       \n32x4乘法器_6_out_4 , \n32x4乘法器_7_out_3 , \n32x4乘法器_7_out_4 , \n32x4乘法器_8_out_3 , \n32x4乘法器_8_out_4 ,
       shifter_1_out, shifter_2_out, shifter_3_out, shifter_4_out, shifter_5_out, shifter_6_out,
       shifter_7_out, shifter_8_out, shifter_9_out, shifter_10_out, shifter_11_out, shifter_12_out,
       shifter_13_out, shifter_14_out;

  \_32X4乘法器  \u_32x4乘法器_1  (.a(a_31_0[31:28]), .b(b_31_0), .out_3(\n32x4乘法器_1_out_3 ), .out_4(\n32x4乘法器_1_out_4 ));
  \_32X4乘法器  \u_32x4乘法器_2  (.a(a_31_0[27:24]), .b(b_31_0), .out_3(\n32x4乘法器_2_out_3 ), .out_4(\n32x4乘法器_2_out_4 ));
  \_32X4乘法器  \u_32x4乘法器_3  (.a(a_31_0[23:20]), .b(b_31_0), .out_3(\n32x4乘法器_3_out_3 ), .out_4(\n32x4乘法器_3_out_4 ));
  \_32X4乘法器  \u_32x4乘法器_4  (.a(a_31_0[19:16]), .b(b_31_0), .out_3(\n32x4乘法器_4_out_3 ), .out_4(\n32x4乘法器_4_out_4 ));
  \_32X4乘法器  \u_32x4乘法器_5  (.a(a_31_0[15:12]), .b(b_31_0), .out_3(\n32x4乘法器_5_out_3 ), .out_4(\n32x4乘法器_5_out_4 ));
  \_32X4乘法器  \u_32x4乘法器_6  (.a(a_31_0[11:8]), .b(b_31_0), .out_3(\n32x4乘法器_6_out_3 ), .out_4(\n32x4乘法器_6_out_4 ));
  \_32X4乘法器  \u_32x4乘法器_7  (.a(a_31_0[7:4]), .b(b_31_0), .out_3(\n32x4乘法器_7_out_3 ), .out_4(\n32x4乘法器_7_out_4 ));
  \_32X4乘法器  \u_32x4乘法器_8  (.a(a_31_0[3:0]), .b(b_31_0), .out_3(\n32x4乘法器_8_out_3 ), .out_4(\n32x4乘法器_8_out_4 ));
  Shifter #(.width(32)) shifter_1 (.in(\n32x4乘法器_1_out_3 ), .\dist (5'b11100), .out(shifter_1_out));
  Shifter #(.width(32)) shifter_2 (.in(\n32x4乘法器_1_out_4 ), .\dist (5'b11100), .out(shifter_2_out));
  Shifter #(.width(32)) shifter_3 (.in(\n32x4乘法器_2_out_3 ), .\dist (5'b11000), .out(shifter_3_out));
  Shifter #(.width(32)) shifter_4 (.in(\n32x4乘法器_2_out_4 ), .\dist (5'b11000), .out(shifter_4_out));
  Shifter #(.width(32)) shifter_5 (.in(\n32x4乘法器_3_out_3 ), .\dist (5'b10100), .out(shifter_5_out));
  Shifter #(.width(32)) shifter_6 (.in(\n32x4乘法器_3_out_4 ), .\dist (5'b10100), .out(shifter_6_out));
  Shifter #(.width(32)) shifter_7 (.in(\n32x4乘法器_4_out_3 ), .\dist (5'b10000), .out(shifter_7_out));
  Shifter #(.width(32)) shifter_8 (.in(\n32x4乘法器_4_out_4 ), .\dist (5'b10000), .out(shifter_8_out));
  Shifter #(.width(32)) shifter_9 (.in(\n32x4乘法器_5_out_3 ), .\dist (5'b01100), .out(shifter_9_out));
  Shifter #(.width(32)) shifter_10 (.in(\n32x4乘法器_5_out_4 ), .\dist (5'b01100), .out(shifter_10_out));
  Shifter #(.width(32)) shifter_11 (.in(\n32x4乘法器_6_out_3 ), .\dist (5'b01000), .out(shifter_11_out));
  Shifter #(.width(32)) shifter_12 (.in(\n32x4乘法器_6_out_4 ), .\dist (5'b01000), .out(shifter_12_out));
  Shifter #(.width(32)) shifter_13 (.in(\n32x4乘法器_7_out_3 ), .\dist (5'b00100), .out(shifter_13_out));
  Shifter #(.width(32)) shifter_14 (.in(\n32x4乘法器_7_out_4 ), .\dist (5'b00100), .out(shifter_14_out));
  Adder #(.width(32)) adder_1 (
    .a(shifter_1_out), .b(shifter_3_out), .out(adder_1_out), .cin(1'b0), .cout(adder_1_cout));
  Adder #(.width(32)) adder_2 (
    .a(adder_1_out), .b(shifter_5_out), .out(adder_2_out), .cin(adder_1_cout), .cout(adder_2_cout));
  Adder #(.width(32)) adder_3 (
    .a(adder_2_out), .b(shifter_7_out), .out(adder_3_out), .cin(adder_2_cout), .cout(adder_3_cout));
  Adder #(.width(32)) adder_4 (
    .a(adder_3_out), .b(shifter_9_out), .out(adder_4_out), .cin(adder_3_cout), .cout(adder_4_cout));
  Adder #(.width(32)) adder_5 (
    .a(adder_4_out), .b(shifter_11_out), .out(adder_5_out), .cin(adder_4_cout), .cout(adder_5_cout));
  Adder #(.width(32)) adder_6 (
    .a(adder_5_out), .b(shifter_13_out), .out(adder_6_out), .cin(adder_5_cout), .cout(adder_6_cout));
  Adder #(.width(32)) adder_7 (
    .a(adder_6_out), .b(\n32x4乘法器_8_out_3 ), .out(p_31_0), .cin(adder_6_cout), .cout(adder_7_cout));
  Adder #(.width(32)) adder_8 (
    .a(shifter_2_out), .b(shifter_4_out), .out(adder_8_out), .cin(adder_7_cout), .cout(adder_8_cout));
  Adder #(.width(32)) adder_9 (
    .a(adder_8_out), .b(shifter_6_out), .out(adder_9_out), .cin(adder_8_cout), .cout(adder_9_cout));
  Adder #(.width(32)) adder_10 (
    .a(adder_9_out), .b(shifter_8_out), .out(adder_10_out), .cin(adder_9_cout), .cout(adder_10_cout));
  Adder #(.width(32)) adder_11 (
    .a(adder_10_out), .b(shifter_10_out), .out(adder_11_out), .cin(adder_10_cout), .cout(adder_11_cout));
  Adder #(.width(32)) adder_12 (
    .a(adder_11_out), .b(shifter_12_out), .out(adder_12_out), .cin(adder_11_cout), .cout(adder_12_cout));
  Adder #(.width(32)) adder_13 (
    .a(adder_12_out), .b(shifter_14_out), .out(adder_13_out), .cin(adder_12_cout), .cout(adder_13_cout));
  Adder #(.width(32)) adder_14 (
    .a(adder_13_out), .b(\n32x4乘法器_8_out_4 ), .out(pc_31_0), .cin(adder_13_cout));  // open: cout
endmodule
