// Logisim project 实验2-CS1806-U201814788-刘美.circ as structural Verilog: 10 circuits, main circuit 四位二进制可逆计数器
module \四位二进制可逆计数器  (
  input  D,
  input  C,
  input  B,
  input  CLR,
  input  LD,
  input  CPU,
  input  CPD,
  input  A,
  output QD,
  output QC,
  output QB,
  output QA
);

  wire and_1_out, and_2_out, and_3_out, and_4_out, and_5_out, and_6_out, and_7_out, and_8_out, and_9_out,
       and_10_out, and_11_out, and_12_out, and_13_out, and_14_out, D0_qn, D1_qn, D2_qn, D3_qn, not_1_out,
       not_2_out, not_3_out, not_4_out, not_5_out, not_6_out, or_1_out, or_2_out, or_3_out, or_4_out,
       or_5_out, or_6_out, or_7_out, or_8_out;

  not not_1 (not_1_out, LD);
  not not_2 (not_2_out, CLR);
  and and_1 (and_1_out, D, not_1_out, not_2_out);
  and and_2 (and_2_out, C, not_2_out, not_1_out);
  and and_3 (and_3_out, B, not_2_out, not_1_out);
  and and_4 (and_4_out, not_2_out, not_1_out, A);
  not not_3 (not_3_out, and_2_out);
  not not_4 (not_4_out, and_3_out);
  not not_5 (not_5_out, and_4_out);
  and and_5 (and_5_out, not_3_out, not_1_out);
  or or_1 (or_1_out, and_5_out, CLR);
  and and_6 (and_6_out, not_4_out, not_1_out);
  or or_2 (or_2_out, and_6_out, CLR);
  or or_3 (or_3_out, CLR, and_7_out);
  and and_7 (and_7_out, not_1_out, not_5_out);
  and and_8 (and_8_out, CPU, QA);
  and and_9 (and_9_out, CPD, D0_qn);
  or or_4 (or_4_out, and_8_out, and_9_out);
  or or_5 (or_5_out, CPU, CPD);
  and and_10 (and_10_out, D1_qn, CPD, D2_qn, D0_qn);
  and and_11 (and_11_out, CPU, QC, QB, QA);
  and and_12 (and_12_out, CPU, QB, QA);
  or or_6 (or_6_out, and_12_out, and_13_out);
  and and_13 (and_13_out, CPD, D0_qn, D1_qn);
  or or_7 (or_7_out, and_10_out, and_11_out);
  not not_6 (not_6_out, and_1_out);
  D_Flip_Flop #(.trigger("falling")) D3 (
    .clk(or_7_out), .D(D3_qn), .Q(QD), .Qn(D3_qn), .preset(and_1_out), .reset(or_8_out));  // open: en
  D_Flip_Flop #(.trigger("falling")) D2 (
    .clk(or_6_out), .D(D2_qn), .Q(QC), .Qn(D2_qn), .preset(and_2_out), .reset(or_1_out));  // open: en
  D_Flip_Flop #(.trigger("falling")) D1 (
    .clk(or_4_out), .D(D1_qn), .Q(QB), .Qn(D1_qn), .preset(and_3_out), .reset(or_2_out));  // open: en
  D_Flip_Flop #(.trigger("falling")) D0 (
    .clk(or_5_out), .D(D0_qn), .Q(QA), .Qn(D0_qn), .preset(and_4_out), .reset(or_3_out));  // open: en
  and and_14 (and_14_out, not_6_out, not_1_out);
  or or_8 (or_8_out, and_14_out, CLR);
endmodule

module \四位二进制可逆计数器测试电路  (
  input  in_1,
  input  in_2,
  input  in_3,
  input  in_4,
  input  in_5,
  output out_6,
  output out_7,
  output out_8,
  output out_9
);

  wire button_1_out, button_2_out, button_3_out;

  Button button_1 (.out(button_1_out));
  Button button_2 (.out(button_2_out));
  Button button_3 (.out(button_3_out));
  \四位二进制可逆计数器  \u_四位二进制可逆计数器_1  (
    .C(in_2), .B(in_3), .CLR(button_2_out), .CPU(button_1_out), .CPD(button_3_out), .A(in_4), .D(in_1),
    .QD(out_6), .QC(out_7), .QB(out_8), .QA(out_9), .LD(in_5));
endmodule

module \二进制8421码电路  (
  input  A3,
  input  A2,
  input  A1,
  input  A0,
  output S7,
  output S6,
  output S5,
  output S4,
  output S3,
  output S2,
  output S1,
  output S0
);

  wire and_1_out, or_1_out;

  or or_1 (or_1_out, A1, A2);
  and and_1 (and_1_out, or_1_out, A3);
  \先行进位的四位二进制并行加法器  \u_先行进位的四位二进制并行加法器_1  (
    .S0(S0), .S1(S1), .S2(S2), .S3(S3), .C4(S4), .C0(1'b0), .A0(A0), .B0(1'b0), .A1(A1), .B1(and_1_out),
    .A2(A2), .B2(and_1_out), .A3(A3), .B3(1'b0));

  assign S5 = 1'b0;
  assign S6 = 1'b0;
  assign S7 = 1'b0;
endmodule

module \二进制8421码测试电路  (
  input  in_1,
  input  in_2,
  input  in_3,
  input  in_4,
  output out_5,
  output out_6,
  output out_7,
  output out_8,
  output out_9,
  output out_10,
  output out_11,
  output out_12
);

  \二进制8421码电路  \u_二进制8421码电路_1  (
    .A3(in_1), .A2(in_2), .A1(in_3), .A0(in_4), .S7(out_5), .S6(out_6), .S5(out_7), .S4(out_8), .S3(out_9),
    .S2(out_10), .S1(out_11), .S0(out_12));
endmodule

module \显示电路  (
  input  A3,
  input  A2,
  input  A1,
  input  A0,
  output g,
  output f,
  output e,
  output d,
  output c,
  output b,
  output a
);

  wire and_1_out, and_2_out, and_3_out, and_4_out, and_5_out, and_6_out, and_7_out, and_8_out, and_9_out,
       and_10_out, and_11_out, and_12_out, and_13_out, and_14_out, and_15_out, and_16_out, and_17_out,
       and_18_out, and_19_out, and_20_out, and_21_out, and_22_out, and_23_out, and_24_out, not_1_out,
       not_2_out, not_3_out, not_4_out;

  not not_1 (not_1_out, A3);
  not not_2 (not_2_out, A2);
  not not_3 (not_3_out, A1);
  not not_4 (not_4_out, A0);
  and and_1 (and_1_out, not_4_out, A1);
  and and_2 (and_2_out, A1, not_2_out);
  and and_3 (and_3_out, not_2_out, A3);
  and and_4 (and_4_out, not_3_out, A2);
  and and_5 (and_5_out, not_4_out, A2);
  and and_6 (and_6_out, not_3_out, not_2_out, A3);
  and and_7 (and_7_out, not_3_out, A2);
  and and_8 (and_8_out, not_4_out, not_3_out);
  and and_9 (and_9_out, not_4_out, not_2_out);
  and and_10 (and_10_out, A1, not_4_out);
  and and_11 (and_11_out, A2, not_1_out);
  and and_12 (and_12_out, A0, A1, not_1_out);
  and and_13 (and_13_out, not_2_out, not_1_out);
  and and_14 (and_14_out, not_1_out, A2, A0);
  and and_15 (and_15_out, not_1_out, not_2_out, A1);
  and and_16 (and_16_out, not_2_out, not_3_out, not_4_out);
  and and_17 (and_17_out, not_3_out, not_4_out);
  and and_18 (and_18_out, not_2_out, not_3_out);
  and and_19 (and_19_out, A2, A1, not_4_out);
  and and_20 (and_20_out, not_2_out, A0);
  and and_21 (and_21_out, not_2_out, not_4_out);
  and and_22 (and_22_out, A1, not_2_out);
  and and_23 (and_23_out, not_3_out, A0, A2);
  and and_24 (and_24_out, A3, not_3_out, A0);
  or or_1 (g, and_1_out, and_2_out, and_3_out, and_4_out);
  or or_2 (f, and_5_out, and_6_out, and_7_out, and_8_out);
  or or_3 (e, and_10_out, and_9_out);
  or or_4 (d, and_23_out, and_22_out, and_21_out, and_19_out);
  or or_5 (c, and_11_out, and_18_out, and_20_out);
  or or_6 (b, and_17_out, and_12_out, and_13_out, and_18_out);
  or or_7 (a, and_14_out, and_15_out, and_16_out, and_24_out);
endmodule

module \显示电路测试电路  (
  input  in_1,
  input  in_2,
  input  in_3,
  input  in_4
);

  wire \显示电路_1_a , \显示电路_1_b , \显示电路_1_c , \显示电路_1_d , \显示电路_1_e , \显示电路_1_f , \显示电路_1_g ;

  \显示电路  \u_显示电路_1  (
    .A3(in_1), .A2(in_2), .A1(in_3), .A0(in_4), .g(\显示电路_1_g ), .f(\显示电路_1_f ), .e(\显示电路_1_e ),
    .d(\显示电路_1_d ), .c(\显示电路_1_c ), .b(\显示电路_1_b ), .a(\显示电路_1_a ));
  _7_Segment_Display u_7_segment_display_1 (
    .g(\显示电路_1_g ), .f(\显示电路_1_f ), .a(\显示电路_1_a ), .b(\显示电路_1_b ), .e(\显示电路_1_e ), .d(\显示电路_1_d ),
    .c(\显示电路_1_c ));  // open: dp
endmodule

module \报警电路  (
  input  CPU,
  input  CLR,
  input  CPD,
  input  in_4,
  input  in_5,
  input  in_6,
  input  in_7,
  input  in_8,
  output QD,
  output QC,
  output QB,
  output QA
);

  wire and_1_out, and_2_out, and_3_out, and_4_out, not_1_out, or_1_out;

  LED led_1 (.in(and_1_out));
  and and_1 (and_1_out, CPU, and_3_out);
  not not_1 (not_1_out, and_3_out);
  and and_2 (and_2_out, not_1_out, CPU);
  and and_3 (and_3_out, QD, QC, QB, QA);
  or or_1 (or_1_out, QD, QC, QB, QA);
  and and_4 (and_4_out, or_1_out, CPD);
  \四位二进制可逆计数器  \u_四位二进制可逆计数器_1  (
    .C(in_5), .B(in_6), .CLR(CLR), .CPU(and_2_out), .CPD(and_4_out), .A(in_7), .D(in_4), .QD(QD), .QC(QC),
    .QB(QB), .QA(QA), .LD(in_8));
endmodule

module \小型实验室门禁系统  (
  input  CPU,
  input  CLR,
  input  CPD,
  output out_4,
  output out_5,
  output out_6,
  output out_7,
  output out_8,
  output out_9,
  output out_10,
  output out_11,
  output out_12,
  output out_13,
  output out_14,
  output out_15,
  output out_16,
  output out_17,
  output LED
);

  wire and_2_out, and_3_out, and_4_out, not_1_out, or_1_out, \二进制8421码电路_1_s0 , \二进制8421码电路_1_s1 ,
       \二进制8421码电路_1_s2 , \二进制8421码电路_1_s3 , \二进制8421码电路_1_s4 , \二进制8421码电路_1_s5 , \二进制8421码电路_1_s6 ,
       \二进制8421码电路_1_s7 , \四位二进制可逆计数器_1_qa , \四位二进制可逆计数器_1_qb , \四位二进制可逆计数器_1_qc , \四位二进制可逆计数器_1_qd ;

  not not_1 (not_1_out, and_3_out);
  and and_1 (LED, CPU, and_3_out);
  and and_2 (and_2_out, not_1_out, CPU);
  \显示电路  \u_显示电路_1  (
    .A3(\二进制8421码电路_1_s7 ), .A2(\二进制8421码电路_1_s6 ), .A1(\二进制8421码电路_1_s5 ), .A0(\二进制8421码电路_1_s4 ),
    .g(out_4), .f(out_5), .e(out_6), .d(out_7), .c(out_8), .b(out_9), .a(out_10));
  and and_3 (and_3_out, \四位二进制可逆计数器_1_qd , \四位二进制可逆计数器_1_qc , \四位二进制可逆计数器_1_qb , \四位二进制可逆计数器_1_qa );
  or or_1 (or_1_out, \四位二进制可逆计数器_1_qd , \四位二进制可逆计数器_1_qc , \四位二进制可逆计数器_1_qb , \四位二进制可逆计数器_1_qa );
  and and_4 (and_4_out, or_1_out, CPD);
  \二进制8421码电路  \u_二进制8421码电路_1  (
    .A3(\四位二进制可逆计数器_1_qd ), .A2(\四位二进制可逆计数器_1_qc ), .A1(\四位二进制可逆计数器_1_qb ), .A0(\四位二进制可逆计数器_1_qa ),
    .S7(\二进制8421码电路_1_s7 ), .S6(\二进制8421码电路_1_s6 ), .S5(\二进制8421码电路_1_s5 ), .S4(\二进制8421码电路_1_s4 ),
    .S3(\二进制8421码电路_1_s3 ), .S2(\二进制8421码电路_1_s2 ), .S1(\二进制8421码电路_1_s1 ), .S0(\二进制8421码电路_1_s0 ));
  \显示电路  \u_显示电路_2  (
    .A3(\二进制8421码电路_1_s3 ), .A2(\二进制8421码电路_1_s2 ), .A1(\二进制8421码电路_1_s1 ), .A0(\二进制8421码电路_1_s0 ),
    .g(out_11), .f(out_12), .e(out_13), .d(out_14), .c(out_15), .b(out_16), .a(out_17));
  \四位二进制可逆计数器  \u_四位二进制可逆计数器_1  (
    .C(1'b0), .B(1'b0), .CLR(CLR), .CPU(and_2_out), .CPD(and_4_out), .A(1'b0), .D(1'b0),
    .QD(\四位二进制可逆计数器_1_qd ), .QC(\四位二进制可逆计数器_1_qc ), .QB(\四位二进制可逆计数器_1_qb ), .QA(\四位二进制可逆计数器_1_qa ), .LD(1'b0));
endmodule

module \小型实验室门禁系统封装测试电路  (
);

  wire button_1_out, button_2_out, button_3_out, \小型实验室门禁系统_1_led , \小型实验室门禁系统_1_out_4 , \小型实验室门禁系统_1_out_5 ,
       \小型实验室门禁系统_1_out_6 , \小型实验室门禁系统_1_out_7 , \小型实验室门禁系统_1_out_8 , \小型实验室门禁系统_1_out_9 ,
       \小型实验室门禁系统_1_out_10 , \小型实验室门禁系统_1_out_11 , \小型实验室门禁系统_1_out_12 , \小型实验室门禁系统_1_out_13 ,
       \小型实验室门禁系统_1_out_14 , \小型实验室门禁系统_1_out_15 , \小型实验室门禁系统_1_out_16 , \小型实验室门禁系统_1_out_17 ;

  Button button_1 (.out(button_1_out));
  Button button_2 (.out(button_2_out));
  Button button_3 (.out(button_3_out));
  _7_Segment_Display u_7_segment_display_1 (
    .g(\小型实验室门禁系统_1_out_4 ), .f(\小型实验室门禁系统_1_out_5 ), .a(\小型实验室门禁系统_1_out_10 ), .b(\小型实验室门禁系统_1_out_9 ),
    .e(\小型实验室门禁系统_1_out_6 ), .d(\小型实验室门禁系统_1_out_7 ), .c(\小型实验室门禁系统_1_out_8 ));  // open: dp
  \小型实验室门禁系统  \u_小型实验室门禁系统_1  (
    .CPU(button_1_out), .CLR(button_2_out), .CPD(button_3_out), .out_4(\小型实验室门禁系统_1_out_4 ),
    .out_5(\小型实验室门禁系统_1_out_5 ), .out_6(\小型实验室门禁系统_1_out_6 ), .out_7(\小型实验室门禁系统_1_out_7 ),
    .out_8(\小型实验室门禁系统_1_out_8 ), .out_9(\小型实验室门禁系统_1_out_9 ), .out_10(\小型实验室门禁系统_1_out_10 ),
    .out_11(\小型实验室门禁系统_1_out_11 ), .out_12(\小型实验室门禁系统_1_out_12 ), .out_13(\小型实验室门禁系统_1_out_13 ),
    .out_14(\小型实验室门禁系统_1_out_14 ), .out_15(\小型实验室门禁系统_1_out_15 ), .out_16(\小型实验室门禁系统_1_out_16 ),
    .out_17(\小型实验室门禁系统_1_out_17 ), .LED(\小型实验室门禁系统_1_led ));
  _7_Segment_Display u_7_segment_display_2 (
    .g(\小型实验室门禁系统_1_out_11 ), .f(\小型实验室门禁系统_1_out_12 ), .a(\小型实验室门禁系统_1_out_17 ), .b(\小型实验室门禁系统_1_out_16 ),
    .e(\小型实验室门禁系统_1_out_13 ), .d(\小型实验室门禁系统_1_out_14 ), .c(\小型实验室门禁系统_1_out_15 ));  // open: dp
  LED led_1 (.in(\小型实验室门禁系统_1_led ));
endmodule

module \先行进位的四位二进制并行加法器  (
  input  C0,
  input  A0,
  input  B0,
  input  A1,
  input  B1,
  input  A2,
  input  B2,
  input  A3,
  input  B3,
  output S2,
  output S3,
  output C4,
  output S0,
  output S1
);

  wire and_1_out, and_2_out, and_3_out, and_4_out, and_5_out, and_6_out, and_7_out, and_8_out, and_9_out,
       and_10_out, and_11_out, and_12_out, and_13_out, and_14_out, or_1_out, or_2_out, or_3_out, xor_2_out,
       xor_4_out, xor_6_out, xor_8_out;

  xor xor_1 (S0, C0, xor_2_out);
  xor xor_2 (xor_2_out, A0, B0);
  or or_1 (or_1_out, and_1_out, and_2_out);
  and and_1 (and_1_out, C0, xor_2_out);
  xor xor_3 (S1, or_1_out, xor_4_out);
  and and_2 (and_2_out, B0, A0);
  xor xor_4 (xor_4_out, A1, B1);
  and and_3 (and_3_out, and_2_out, xor_4_out);
  and and_4 (and_4_out, C0, xor_2_out, xor_4_out);
  xor xor_5 (S2, or_2_out, xor_6_out);
  or or_2 (or_2_out, and_4_out, and_3_out, and_5_out);
  and and_5 (and_5_out, B1, A1);
  or or_3 (or_3_out, and_6_out, and_7_out, and_8_out, and_9_out);
  and and_6 (and_6_out, C0, xor_2_out, xor_4_out, xor_6_out);
  xor xor_6 (xor_6_out, A2, B2);
  xor xor_7 (S3, or_3_out, xor_8_out);
  and and_7 (and_7_out, and_2_out, xor_4_out, xor_6_out);
  and and_8 (and_8_out, and_5_out, xor_6_out);
  and and_9 (and_9_out, B2, A2);
  and and_10 (and_10_out, C0, xor_2_out, xor_4_out, xor_6_out, xor_8_out);
  and and_11 (and_11_out, and_2_out, xor_4_out, xor_6_out, xor_8_out);
  xor xor_8 (xor_8_out, A3, B3);
  or or_4 (C4, and_10_out, and_11_out, and_12_out, and_13_out, and_14_out);
  and and_12 (and_12_out, and_5_out, xor_6_out, xor_8_out);
  and and_13 (and_13_out, and_9_out, xor_8_out);
  and and_14 (and_14_out, B3, A3);
endmodule
