// Logisim project 实验5-CS1806-U201814788-刘美.circ as structural Verilog: 13 circuits, main circuit 六十进制计数器
module \六十进制计数器  (
  input  CPu,
  input  CLR,
  input  CPd,
  input  Adj,
  output Q0d,
  output Q0c,
  output Q0b,
  output Q0a,
  output Q1d,
  output Q1c,
  output Q1b,
  output Q1a,
  output Qcc
);

  wire and_1_out, and_2_out, and_4_out, CF_out, nand_1_out, not_1_out, not_2_out, not_3_out, not_4_out,
       or_1_out, or_2_out, or_3_out, or_4_out;

  or or_1 (or_1_out, CLR, CF_out, and_4_out);
  and and_1 (and_1_out, CPd, or_2_out, Adj);
  not not_1 (not_1_out, Adj);
  or or_2 (or_2_out, Q0a, Q0b, Q0c, Q0d, Q1d, Q1c, Q1b, Q1a);
  \四位二进制可逆计数器  \u_四位二进制可逆计数器_1  (
    .C(1'b0), .B(1'b0), .CLR(or_1_out), .CPU(CPu), .CPD(and_1_out), .A(1'b1), .D(1'b1), .QD(Q0d), .QC(Q0c),
    .QB(Q0b), .QA(Q0a), .LD(nand_1_out));
  not not_2 (not_2_out, Q0a);
  not not_3 (not_3_out, Q0c);
  and CF (CF_out, not_2_out, Q0b, not_3_out, Q0d);
  or or_3 (or_3_out, Q0d, Q0c, Q0b, Q0a);
  not not_4 (not_4_out, or_3_out);
  and and_2 (and_2_out, not_4_out, and_1_out);
  nand nand_1 (nand_1_out, Q0d, Q0c, Q0b, Q0a);
  or or_4 (or_4_out, CLR, and_4_out);
  \四位二进制可逆计数器  \u_四位二进制可逆计数器_2  (
    .C(1'b0), .B(1'b0), .CLR(or_4_out), .CPU(CF_out), .CPD(and_2_out), .A(1'b0), .D(1'b0), .QD(Q1d),
    .QC(Q1c), .QB(Q1b), .QA(Q1a), .LD(1'b1));
  and and_3 (Qcc, Q1b, not_1_out, Q1c);
  and and_4 (and_4_out, Q1b, Q1c);
endmodule

module \六十进制计数器测试电路  (
  input  in_1,
  input  in_2,
  output out_3
);

  wire button_1_out, button_2_out;
  wire [3:0] \六十进制计数器_1_q0a , \六十进制计数器_1_q1a ;

  Button button_1 (.out(button_1_out));
  Button button_2 (.out(button_2_out));
  Hex_Digit_Display hex_digit_display_1 (.value(\六十进制计数器_1_q1a ));  // open: dp
  Hex_Digit_Display hex_digit_display_2 (.value(\六十进制计数器_1_q0a ));  // open: dp
  \六十进制计数器  \u_六十进制计数器_1  (
    .Qcc(out_3), .Q0d(\六十进制计数器_1_q0a [3]), .Q0c(\六十进制计数器_1_q0a [2]), .Q0b(\六十进制计数器_1_q0a [1]),
    .Q0a(\六十进制计数器_1_q0a [0]), .Q1d(\六十进制计数器_1_q1a [3]), .Q1c(\六十进制计数器_1_q1a [2]), .Q1b(\六十进制计数器_1_q1a [1]),
    .Q1a(\六十进制计数器_1_q1a [0]), .CPu(button_1_out), .CLR(in_2), .CPd(button_2_out), .Adj(in_1));
endmodule

module \十二进制计数器或二十四进制的计数器  (
  input  Set,
  input  CPu,
  input  CLR,
  input  CPd,
  input  Adj,
  output out_6,
  output out_7,
  output out_8,
  output out_9,
  output out_10,
  output out_11,
  output out_12,
  output out_13,
  output Qcc
);

  wire and_1_out, and_2_out, and_3_out, and_4_out, CF_out, nand_1_out, not_1_out, not_2_out, not_3_out,
       not_4_out, or_1_out, or_2_out, or_3_out, or_4_out;

  or or_1 (or_1_out, CLR, CF_out, Qcc);
  and and_1 (and_1_out, CPd, or_2_out, Adj);
  or or_2 (or_2_out, out_6, out_7, out_8, out_9, out_10, out_11, out_12, out_13);
  not not_1 (not_1_out, out_9);
  not not_2 (not_2_out, out_7);
  \四位二进制可逆计数器  \u_四位二进制可逆计数器_1  (
    .C(1'b0), .B(1'b0), .CLR(or_1_out), .CPU(CPu), .CPD(and_1_out), .A(1'b1), .D(1'b1), .QD(out_6),
    .QC(out_7), .QB(out_8), .QA(out_9), .LD(nand_1_out));
  or or_3 (or_3_out, out_9, out_8, out_7, out_6);
  nand nand_1 (nand_1_out, out_9, out_8, out_7, out_6);
  and CF (CF_out, not_1_out, out_8, not_2_out, out_6);
  not not_3 (not_3_out, or_3_out);
  and and_2 (and_2_out, not_3_out, and_1_out);
  or or_4 (or_4_out, CLR, Qcc);
  \四位二进制可逆计数器  \u_四位二进制可逆计数器_2  (
    .C(1'b0), .B(1'b0), .CLR(or_4_out), .CPU(CF_out), .CPD(and_2_out), .A(1'b0), .D(1'b0), .QD(out_10),
    .QC(out_11), .QB(out_12), .QA(out_13), .LD(1'b1));
  not not_4 (not_4_out, Set);
  and and_3 (and_3_out, out_7, out_12, Set);
  and and_4 (and_4_out, not_4_out, out_13, out_8);
  or or_5 (Qcc, and_3_out, and_4_out);
endmodule

module \十二进制计数器或二十四进制的计数器测试电路  (
  input  in_1,
  input  in_2,
  input  in_3,
  output out_4
);

  wire button_1_out, button_2_out;
  wire [3:0] \十二进制计数器或二十四进制的计数器_1_out_9 , \十二进制计数器或二十四进制的计数器_1_out_13 ;

  Button button_1 (.out(button_1_out));
  Button button_2 (.out(button_2_out));
  Hex_Digit_Display hex_digit_display_1 (.value(\十二进制计数器或二十四进制的计数器_1_out_13 ));  // open: dp
  Hex_Digit_Display hex_digit_display_2 (.value(\十二进制计数器或二十四进制的计数器_1_out_9 ));  // open: dp
  \十二进制计数器或二十四进制的计数器  \u_十二进制计数器或二十四进制的计数器_1  (
    .Qcc(out_4), .CLR(in_3), .CPd(button_2_out), .Adj(in_1), .CPu(button_1_out), .Set(in_2),
    .out_6(\十二进制计数器或二十四进制的计数器_1_out_9 [3]), .out_7(\十二进制计数器或二十四进制的计数器_1_out_9 [2]),
    .out_8(\十二进制计数器或二十四进制的计数器_1_out_9 [1]), .out_9(\十二进制计数器或二十四进制的计数器_1_out_9 [0]),
    .out_10(\十二进制计数器或二十四进制的计数器_1_out_13 [3]), .out_11(\十二进制计数器或二十四进制的计数器_1_out_13 [2]),
    .out_12(\十二进制计数器或二十四进制的计数器_1_out_13 [1]), .out_13(\十二进制计数器或二十四进制的计数器_1_out_13 [0]));
endmodule

module \上下午文字显示的电路  (
  input  TT,
  input  AM_FM,
  output [4:0] out_3,
  output [4:0] out_4,
  output [4:0] out_5,
  output [4:0] out_6
);

  wire [19:0] multiplexer_1_out;

  Multiplexer #(.width(20)) multiplexer_1 (
    .in0(20'hfca1), .in1(20'h87e90), .out(multiplexer_1_out), .sel(AM_FM));  // open: en
  Multiplexer #(.width(20)) multiplexer_2 (
    .in0({20{1'b0}}), .in1(multiplexer_1_out), .out({out_3, out_4, out_5, out_6}), .sel(TT));  // open: en
endmodule

module \上下午文字显示测试电路  (
  input  in_1,
  input  in_2
);

  wire [4:0] \上下午文字显示的电路_1_out_3 , \上下午文字显示的电路_1_out_4 , \上下午文字显示的电路_1_out_5 , \上下午文字显示的电路_1_out_6 ;

  \上下午文字显示的电路  \u_上下午文字显示的电路_1  (
    .out_3(\上下午文字显示的电路_1_out_3 ), .out_4(\上下午文字显示的电路_1_out_4 ), .out_5(\上下午文字显示的电路_1_out_5 ),
    .out_6(\上下午文字显示的电路_1_out_6 ), .AM_FM(in_1), .TT(in_2));
  DotMatrix #(.matrixcols(4), .matrixrows(5)) dotmatrix_1 (
    .col0(\上下午文字显示的电路_1_out_3 ), .col1(\上下午文字显示的电路_1_out_4 ), .col2(\上下午文字显示的电路_1_out_5 ),
    .col3(\上下午文字显示的电路_1_out_6 ));
endmodule

module \电子钟整点报时电路  (
  input  in_1,
  input  in_2,
  input  in_3,
  input  in_4,
  input  in_5,
  input  \分 ,
  input  in_7,
  input  in_8,
  input  in_9,
  input  in_10,
  input  in_11,
  input  in_12,
  input  in_13,
  input  \秒 ,
  input  in_15,
  input  in_16,
  input  in_17,
  output out_18
);

  wire not_1_out, not_2_out, not_3_out, not_4_out, not_5_out, not_6_out;

  not not_1 (not_1_out, in_7);
  not not_2 (not_2_out, in_8);
  not not_3 (not_3_out, in_10);
  not not_4 (not_4_out, in_12);
  not not_5 (not_5_out, in_2);
  not not_6 (not_6_out, in_4);
  and and_1 (out_18, not_5_out, in_3, not_6_out, in_5, \分 , not_1_out, in_1, not_2_out, in_9, not_3_out, in_11, not_4_out, in_13);

  assign in_16 = in_15;
  assign in_17 = in_15;
  assign \秒  = in_15;
  // also tied to GND on the sheet: in_15
endmodule

module \电子钟整点报时电路测试电路  (
  input  in_1,
  input  in_2,
  input  in_3,
  input  in_4,
  input  in_5,
  input  in_6,
  input  in_7,
  input  in_8,
  input  in_9,
  input  in_10,
  input  in_11,
  input  in_12,
  input  in_13,
  input  in_14,
  input  in_15,
  input  in_16,
  input  in_17
);

  wire \电子钟整点报时电路_1_out_18 ;

  \电子钟整点报时电路  \u_电子钟整点报时电路_1  (
    .\分 (in_14), .in_7(in_15), .in_8(in_16), .in_9(in_17), .in_2(in_10), .in_3(in_11), .in_4(in_12),
    .in_5(in_13), .in_10(in_2), .in_11(in_3), .in_12(in_4), .in_13(in_5), .out_18(\电子钟整点报时电路_1_out_18 ),
    .\秒 (in_6), .in_15(in_7), .in_16(in_8), .in_17(in_9), .in_1(in_1));
  LED led_1 (.in(\电子钟整点报时电路_1_out_18 ));
endmodule

module \秒脉冲产生电路  (
  input  in_1,
  output out_2
);

  wire \四位二进制可逆计数器_1_qa , \四位二进制可逆计数器_1_qb , \四位二进制可逆计数器_1_qc ;

  and and_1 (out_2, \四位二进制可逆计数器_1_qc , \四位二进制可逆计数器_1_qb , \四位二进制可逆计数器_1_qa );
  \四位二进制可逆计数器  \u_四位二进制可逆计数器_1  (
    .C(1'b0), .B(1'b0), .CLR(out_2), .CPU(in_1), .CPD(1'b0), .A(1'b0), .D(1'b0), .QC(\四位二进制可逆计数器_1_qc ),
    .QB(\四位二进制可逆计数器_1_qb ), .QA(\四位二进制可逆计数器_1_qa ), .LD(1'b1));  // open: QD
endmodule

module \多功能数字钟  (
  input  CPu,
  input  CPd,
  input  Clr,
  input  Set,
  input  CP,
  input  Adj0,
  input  Adj1,
  output out_8,
  output [3:0] out_9,
  output [3:0] out_10,
  output [3:0] out_11,
  output [3:0] out_12,
  output [3:0] out_13,
  output [3:0] out_14,
  output [4:0] out_15,
  output [4:0] out_16,
  output [4:0] out_17,
  output [4:0] out_18
);

  wire and_1_out, and_2_out, and_3_out, and_4_out, and_5_out, and_6_out, and_7_out, comparator_1_eq,
       comparator_1_gt, comparator_2_eq, not_1_out, not_2_out, not_3_out, not_4_out, or_1_out, or_2_out,
       or_3_out, \分计时_qcc , \秒脉冲产生电路_1_out_2 , \秒计时_qcc ;
  wire [7:0] multiplexer_1_out, multiplexer_2_out, multiplexer_4_out, subtractor_1_out,
       \十二进制计数器或二十四进制的计数器_1_out_9 ;

  and and_1 (and_1_out, CP, not_1_out);
  \六十进制计数器  \u_秒计时  (
    .Qcc(\秒计时_qcc ), .Q0d(out_14[3]), .Q0c(out_14[2]), .Q0b(out_14[1]), .Q0a(out_14[0]), .Q1d(out_13[3]),
    .Q1c(out_13[2]), .Q1b(out_13[1]), .Q1a(out_13[0]), .CPu(\秒脉冲产生电路_1_out_2 ), .CLR(Clr), .CPd(1'b0),
    .Adj(1'b0));
  and and_2 (and_2_out, CPu, and_3_out);
  \秒脉冲产生电路  \u_秒脉冲产生电路_1  (.in_1(and_1_out), .out_2(\秒脉冲产生电路_1_out_2 ));
  or or_1 (or_1_out, and_2_out, \秒计时_qcc );
  and and_3 (and_3_out, Adj0, Adj1);
  \电子钟整点报时电路  \u_电子钟整点报时电路_1  (
    .\分 (out_12[3]), .in_7(out_12[2]), .in_8(out_12[1]), .in_9(out_12[0]), .in_2(out_11[3]),
    .in_3(out_11[2]), .in_4(out_11[1]), .in_5(out_11[0]), .in_10(out_13[3]), .in_11(out_13[2]),
    .in_12(out_13[1]), .in_13(out_13[0]), .out_18(out_8), .\秒 (out_14[3]), .in_15(out_14[2]),
    .in_16(out_14[1]), .in_17(out_14[0]), .in_1(not_1_out));
  not not_1 (not_1_out, Adj0);
  not not_2 (not_2_out, Adj1);
  and and_4 (and_4_out, CPu, and_6_out);
  and and_5 (and_5_out, not_1_out, \分计时_qcc );
  \六十进制计数器  \u_分计时  (
    .Qcc(\分计时_qcc ), .Q0d(out_12[3]), .Q0c(out_12[2]), .Q0b(out_12[1]), .Q0a(out_12[0]), .Q1d(out_11[3]),
    .Q1c(out_11[2]), .Q1b(out_11[1]), .Q1a(out_11[0]), .CPu(or_1_out), .CLR(Clr), .CPd(CPd), .Adj(and_3_out));
  or or_2 (or_2_out, and_4_out, and_5_out);
  and and_6 (and_6_out, not_2_out, Adj0);
  Multiplexer #(.width(8)) multiplexer_1 (
    .in0(8'h12), .in1(8'h18), .out(multiplexer_1_out), .sel(and_7_out));  // open: en
  and and_7 (and_7_out, \十二进制计数器或二十四进制的计数器_1_out_9 [5], not_3_out);
  not not_3 (not_3_out, \十二进制计数器或二十四进制的计数器_1_out_9 [1]);
  Subtractor subtractor_1 (
    .a(\十二进制计数器或二十四进制的计数器_1_out_9 ), .b(multiplexer_1_out), .out(subtractor_1_out));  // open: bin, bout
  Comparator comparator_1 (
    .a(\十二进制计数器或二十四进制的计数器_1_out_9 ), .b(8'h12), .gt(comparator_1_gt), .eq(comparator_1_eq));  // open: lt
  \十二进制计数器或二十四进制的计数器  \u_十二进制计数器或二十四进制的计数器_1  (
    .CLR(Clr), .CPd(CPd), .Adj(and_6_out), .CPu(or_2_out), .Set(1'b1),
    .out_6(\十二进制计数器或二十四进制的计数器_1_out_9 [3]), .out_7(\十二进制计数器或二十四进制的计数器_1_out_9 [2]),
    .out_8(\十二进制计数器或二十四进制的计数器_1_out_9 [1]), .out_9(\十二进制计数器或二十四进制的计数器_1_out_9 [0]),
    .out_10(\十二进制计数器或二十四进制的计数器_1_out_9 [7]), .out_11(\十二进制计数器或二十四进制的计数器_1_out_9 [6]),
    .out_12(\十二进制计数器或二十四进制的计数器_1_out_9 [5]), .out_13(\十二进制计数器或二十四进制的计数器_1_out_9 [4]));  // open: Qcc
  or or_3 (or_3_out, comparator_1_gt, comparator_1_eq);
  Multiplexer #(.width(8)) multiplexer_2 (
    .in0(\十二进制计数器或二十四进制的计数器_1_out_9 ), .in1(subtractor_1_out), .out(multiplexer_2_out), .sel(or_3_out));  // open: en
  Comparator comparator_2 (.a(multiplexer_2_out), .b({8{1'b0}}), .eq(comparator_2_eq));  // open: gt, lt
  Multiplexer #(.width(8)) multiplexer_3 (
    .in0(multiplexer_4_out), .in1(\十二进制计数器或二十四进制的计数器_1_out_9 ), .out({out_9, out_10}), .sel(Set));  // open: en
  Multiplexer #(.width(8)) multiplexer_4 (
    .in0(multiplexer_2_out), .in1(8'h12), .out(multiplexer_4_out), .sel(comparator_2_eq));  // open: en
  not not_4 (not_4_out, Set);
  \上下午文字显示的电路  \u_上下午文字显示的电路_1  (
    .out_3(out_15), .out_4(out_16), .out_5(out_17), .out_6(out_18), .AM_FM(or_3_out), .TT(not_4_out));
endmodule

module \多功能数字钟测试电路  (
  input  in_1,
  input  in_2,
  input  in_3,
  input  in_4
);

  wire button_1_out, button_2_out, clock_1_out, \多功能数字钟_1_out_8 ;
  wire [3:0] \多功能数字钟_1_out_9 , \多功能数字钟_1_out_10 , \多功能数字钟_1_out_11 , \多功能数字钟_1_out_12 , \多功能数字钟_1_out_13 ,
       \多功能数字钟_1_out_14 ;
  wire [4:0] \多功能数字钟_1_out_15 , \多功能数字钟_1_out_16 , \多功能数字钟_1_out_17 , \多功能数字钟_1_out_18 ;

  DotMatrix #(.matrixcols(4), .matrixrows(5)) dotmatrix_1 (
    .col0(\多功能数字钟_1_out_15 ), .col1(\多功能数字钟_1_out_16 ), .col2(\多功能数字钟_1_out_17 ), .col3(\多功能数字钟_1_out_18 ));
  Clock clock_1 (.out(clock_1_out));
  Hex_Digit_Display hex_digit_display_1 (.value(\多功能数字钟_1_out_9 ));  // open: dp
  Button button_1 (.out(button_1_out));
  Button button_2 (.out(button_2_out));
  Hex_Digit_Display hex_digit_display_2 (.value(\多功能数字钟_1_out_10 ));  // open: dp
  Hex_Digit_Display hex_digit_display_3 (.value(\多功能数字钟_1_out_11 ));  // open: dp
  Hex_Digit_Display hex_digit_display_4 (.value(\多功能数字钟_1_out_12 ));  // open: dp
  Hex_Digit_Display hex_digit_display_5 (.value(\多功能数字钟_1_out_13 ));  // open: dp
  Hex_Digit_Display hex_digit_display_6 (.value(\多功能数字钟_1_out_14 ));  // open: dp
  \多功能数字钟  \u_多功能数字钟_1  (
    .out_15(\多功能数字钟_1_out_15 ), .out_16(\多功能数字钟_1_out_16 ), .out_17(\多功能数字钟_1_out_17 ),
    .out_18(\多功能数字钟_1_out_18 ), .out_13(\多功能数字钟_1_out_13 ), .CPu(button_1_out), .CP(clock_1_out),
    .CPd(button_2_out), .Adj0(in_1), .Adj1(in_2), .Clr(in_4), .Set(in_3), .out_14(\多功能数字钟_1_out_14 ),
    .out_11(\多功能数字钟_1_out_11 ), .out_12(\多功能数字钟_1_out_12 ), .out_10(\多功能数字钟_1_out_10 ),
    .out_9(\多功能数字钟_1_out_9 ), .out_8(\多功能数字钟_1_out_8 ));
  LED led_1 (.in(\多功能数字钟_1_out_8 ));
endmodule

module \闹钟测试电路  (
  input  in_1,
  input  in_2,
  input  in_3,
  input  in_4,
  input  in_5,
  input  in_6
);

  wire button_1_out, button_2_out, clock_1_out, \闹钟_1_out_20 , \闹钟_1_out_21 ;
  wire [3:0] \闹钟_1_out_10 , \闹钟_1_out_11 , \闹钟_1_out_12 , \闹钟_1_out_13 , \闹钟_1_out_14 , \闹钟_1_out_15 ;
  wire [4:0] \闹钟_1_out_16 , \闹钟_1_out_17 , \闹钟_1_out_18 , \闹钟_1_out_19 ;

  DotMatrix #(.matrixcols(4), .matrixrows(5)) dotmatrix_1 (
    .col0(\闹钟_1_out_16 ), .col1(\闹钟_1_out_17 ), .col2(\闹钟_1_out_18 ), .col3(\闹钟_1_out_19 ));
  \闹钟  \u_闹钟_1  (
    .in_2(in_1), .in_3(in_2), .out_16(\闹钟_1_out_16 ), .out_17(\闹钟_1_out_17 ), .out_18(\闹钟_1_out_18 ),
    .in_5(button_1_out), .in_6(button_2_out), .in_7(in_3), .in_8(in_4), .out_20(\闹钟_1_out_20 ),
    .out_21(\闹钟_1_out_21 ), .in_1(in_5), .Clockadj(in_6), .out_10(\闹钟_1_out_10 ), .out_11(\闹钟_1_out_11 ),
    .out_12(\闹钟_1_out_12 ), .out_13(\闹钟_1_out_13 ), .out_14(\闹钟_1_out_14 ), .out_15(\闹钟_1_out_15 ),
    .in_4(clock_1_out), .out_19(\闹钟_1_out_19 ));
  Clock clock_1 (.out(clock_1_out));
  Button button_1 (.out(button_1_out));
  Button button_2 (.out(button_2_out));
  Hex_Digit_Display hex_digit_display_1 (.value(\闹钟_1_out_11 ));  // open: dp
  Hex_Digit_Display hex_digit_display_2 (.value(\闹钟_1_out_10 ));  // open: dp
  Hex_Digit_Display hex_digit_display_3 (.value(\闹钟_1_out_13 ));  // open: dp
  Hex_Digit_Display hex_digit_display_4 (.value(\闹钟_1_out_12 ));  // open: dp
  Hex_Digit_Display hex_digit_display_5 (.value(\闹钟_1_out_15 ));  // open: dp
  Hex_Digit_Display hex_digit_display_6 (.value(\闹钟_1_out_14 ));  // open: dp
  LED led_1 (.in(\闹钟_1_out_20 ));
  LED led_2 (.in(\闹钟_1_out_21 ));

  // Notes on the sheet:
  //   Clock=0表示关闭闹钟，为1表示开启闹钟
  //   ClockAdj为0表示不调整闹钟，为1表示调整闹钟，调整尽在闹钟开启时有效
endmodule

module \闹钟  (
  input  in_1,
  input  in_2,
  input  in_3,
  input  in_4,
  input  in_5,
  input  in_6,
  input  in_7,
  input  in_8,
  input  Clockadj,
  output [3:0] out_10,
  output [3:0] out_11,
  output [3:0] out_12,
  output [3:0] out_13,
  output [3:0] out_14,
  output [3:0] out_15,
  output [4:0] out_16,
  output [4:0] out_17,
  output [4:0] out_18,
  output [4:0] out_19,
  output out_20,
  output out_21
);

  wire and_1_out, and_2_out, and_3_out, and_4_out, and_5_out, and_7_out, comparator_1_eq, comparator_2_eq,
       multiplexer_5_out, nand_1_out, \四位二进制可逆计数器_1_qb , \四位二进制可逆计数器_1_qd , \多功能数字钟_2_out_8 ,
       \秒脉冲产生电路_1_out_2 ;
  wire [3:0] \多功能数字钟_2_out_11 , \多功能数字钟_2_out_12 , \多功能数字钟_2_out_13 , \多功能数字钟_2_out_14 ;
  wire [4:0] \多功能数字钟_1_out_15 , \多功能数字钟_1_out_16 , \多功能数字钟_1_out_17 , \多功能数字钟_1_out_18 ;
  wire [7:0] \多功能数字钟_1_out_14 , \多功能数字钟_2_out_10 ;
  wire [15:0] \多功能数字钟_1_out_12 ;
  wire [19:0] \多功能数字钟_2_out_18 ;
  wire [23:8] multiplexer_4_out;

  Multiplexer #(.width(24)) multiplexer_1 (
    .in0({\多功能数字钟_1_out_12 , \多功能数字钟_1_out_14 }), .in1({multiplexer_4_out, {8{1'b0}}}),
    .out({out_10, out_11, out_12, out_13, out_14, out_15}), .sel(and_1_out));  // open: en
  and and_1 (and_1_out, Clockadj, in_1);
  Comparator #(.width(20)) comparator_1 (
    .a({\多功能数字钟_1_out_15 , \多功能数字钟_1_out_16 , \多功能数字钟_1_out_17 , \多功能数字钟_1_out_18 }), .b(\多功能数字钟_2_out_18 ),
    .eq(comparator_1_eq));  // open: gt, lt
  and and_2 (and_2_out, in_1, Clockadj);
  \多功能数字钟  \u_多功能数字钟_1  (
    .out_15(\多功能数字钟_1_out_15 ), .out_16(\多功能数字钟_1_out_16 ), .out_17(\多功能数字钟_1_out_17 ),
    .out_18(\多功能数字钟_1_out_18 ), .out_13(\多功能数字钟_1_out_14 [7:4]), .CPu(in_5), .CP(in_4), .CPd(in_6),
    .Adj0(in_2), .Adj1(in_3), .Clr(in_8), .Set(in_7), .out_14(\多功能数字钟_1_out_14 [3:0]),
    .out_11(\多功能数字钟_1_out_12 [7:4]), .out_12(\多功能数字钟_1_out_12 [3:0]), .out_10(\多功能数字钟_1_out_12 [11:8]),
    .out_9(\多功能数字钟_1_out_12 [15:12]), .out_8(out_20));
  Multiplexer #(.width(20)) multiplexer_2 (
    .in0({\多功能数字钟_1_out_15 , \多功能数字钟_1_out_16 , \多功能数字钟_1_out_17 , \多功能数字钟_1_out_18 }),
    .in1(\多功能数字钟_2_out_18 ), .out({out_16, out_17, out_18, out_19}), .sel(and_2_out));  // open: en
  and and_3 (and_3_out, Clockadj, in_3);
  Multiplexer #(.width(8)) multiplexer_3 (
    .in0({8{1'b0}}), .in1(\多功能数字钟_2_out_10 ), .out(multiplexer_4_out[23:16]), .sel(in_1));  // open: en
  and and_4 (and_4_out, Clockadj, in_5, in_1);
  and and_5 (and_5_out, Clockadj, in_6, in_1);
  \多功能数字钟  \u_多功能数字钟_2  (
    .out_15(\多功能数字钟_2_out_18 [19:15]), .out_16(\多功能数字钟_2_out_18 [14:10]), .out_17(\多功能数字钟_2_out_18 [9:5]),
    .out_18(\多功能数字钟_2_out_18 [4:0]), .out_13(\多功能数字钟_2_out_13 ), .CPu(and_4_out), .CP(1'b0), .CPd(and_5_out),
    .Adj0(in_1), .Adj1(and_3_out), .Clr(1'b0), .Set(in_7), .out_14(\多功能数字钟_2_out_14 ),
    .out_11(\多功能数字钟_2_out_11 ), .out_12(\多功能数字钟_2_out_12 ), .out_10(\多功能数字钟_2_out_10 [3:0]),
    .out_9(\多功能数字钟_2_out_10 [7:4]), .out_8(\多功能数字钟_2_out_8 ));
  Multiplexer #(.width(8)) multiplexer_4 (
    .in0({8{1'b0}}), .in1({\多功能数字钟_2_out_11 , \多功能数字钟_2_out_12 }), .out(multiplexer_4_out[15:8]), .sel(in_1));  // open: en
  and and_6 (out_21, in_1, in_4, nand_1_out, and_7_out);
  nand nand_1 (nand_1_out, \四位二进制可逆计数器_1_qb , \四位二进制可逆计数器_1_qd );
  \秒脉冲产生电路  \u_秒脉冲产生电路_1  (.in_1(in_4), .out_2(\秒脉冲产生电路_1_out_2 ));
  Comparator #(.width(16)) comparator_2 (
    .a(\多功能数字钟_1_out_12 ), .b({\多功能数字钟_2_out_10 , \多功能数字钟_2_out_11 , \多功能数字钟_2_out_12 }), .eq(comparator_2_eq));  // open: gt, lt
  and and_7 (and_7_out, comparator_2_eq, comparator_1_eq, nand_1_out);
  \四位二进制可逆计数器  \u_四位二进制可逆计数器_1  (
    .C(1'b0), .B(1'b0), .CLR(1'b0), .CPU(multiplexer_5_out), .CPD(1'b0), .A(1'b0), .D(1'b0),
    .QD(\四位二进制可逆计数器_1_qd ), .QB(\四位二进制可逆计数器_1_qb ), .LD(1'b1));  // open: QC, QA
  Multiplexer multiplexer_5 (
    .in0(1'b0), .in1(\秒脉冲产生电路_1_out_2 ), .out(multiplexer_5_out), .sel(and_7_out));  // open: en
  // also tied to GND on the sheet: {\多功能数字钟_2_out_13 [0], \多功能数字钟_2_out_13 [1], \多功能数字钟_2_out_13 [2], \多功能数字钟_2_out_13 [3], \多功能数字钟_2_out_14 [0], \多功能数字钟_2_out_14 [1], \多功能数字钟_2_out_14 [2], \多功能数字钟_2_out_14 [3], \多功能数字钟_2_out_8 }
endmodule
