// Logisim project 实验4-CS1806-U201814788-刘美.circ as structural Verilog: 5 circuits, main circuit 四位除法器
module \四位除法器  (
  input  [3:0] n2,
  input  [3:0] d,
  output [3:0] quot,
  output [3:0] rem
);

  wire comparator_1_eq, comparator_1_gt, comparator_2_eq, comparator_2_gt, comparator_3_eq, comparator_3_gt,
       comparator_4_eq, comparator_4_gt, or_1_out, or_2_out, or_3_out, or_4_out;
  wire [0:0] multiplexer_1_out, multiplexer_3_out;
  wire [3:0] multiplexer_2_out, multiplexer_4_out, subtractor_1_out, subtractor_2_out, subtractor_3_out,
       subtractor_4_out;
  wire [7:0] bit_extender_1_out, multiplexer_7_out, shifter_1_out, shifter_2_out, shifter_3_out,
       shifter_4_out;

  assign bit_extender_1_out = {{4{1'b0}}, n2};  // Bit_Extender bit_extender_1
  Shifter shifter_1 (
    .in(bit_extender_1_out), .\dist (3'b001),
    .out({shifter_1_out[7:4], multiplexer_7_out[3:1], shifter_1_out[0]}));
  Shifter shifter_2 (.in(multiplexer_7_out), .\dist (3'b001), .out(shifter_2_out));
  Shifter shifter_3 (
    .in({multiplexer_2_out, shifter_2_out[3:1], multiplexer_1_out[0]}), .\dist (3'b001), .out(shifter_3_out));
  Shifter shifter_4 (
    .in({multiplexer_4_out, shifter_3_out[3:1], multiplexer_3_out[0]}), .\dist (3'b001),
    .out({shifter_4_out[7:4], quot[3:1], shifter_4_out[0]}));
  Comparator #(.width(4), .mode("unsigned")) comparator_1 (
    .a(shifter_1_out[7:4]), .b(d), .gt(comparator_1_gt), .eq(comparator_1_eq));  // open: lt
  Subtractor #(.width(4)) subtractor_1 (.a(shifter_1_out[7:4]), .b(d), .out(subtractor_1_out));  // open: bin, bout
  Comparator #(.width(4), .mode("unsigned")) comparator_2 (
    .a(shifter_2_out[7:4]), .b(d), .gt(comparator_2_gt), .eq(comparator_2_eq));  // open: lt
  Subtractor #(.width(4)) subtractor_2 (.a(shifter_2_out[7:4]), .b(d), .out(subtractor_2_out));  // open: bin, bout
  Comparator #(.width(4), .mode("unsigned")) comparator_3 (
    .a(shifter_3_out[7:4]), .b(d), .gt(comparator_3_gt), .eq(comparator_3_eq));  // open: lt
  Subtractor #(.width(4)) subtractor_3 (.a(shifter_3_out[7:4]), .b(d), .out(subtractor_3_out));  // open: bin, bout
  Comparator #(.width(4), .mode("unsigned")) comparator_4 (
    .a(shifter_4_out[7:4]), .b(d), .gt(comparator_4_gt), .eq(comparator_4_eq));  // open: lt
  Subtractor #(.width(4)) subtractor_4 (.a(shifter_4_out[7:4]), .b(d), .out(subtractor_4_out));  // open: bin, bout
  or or_1 (or_1_out, comparator_1_gt, comparator_1_eq);
  or or_2 (or_2_out, comparator_2_gt, comparator_2_eq);
  or or_3 (or_3_out, comparator_3_gt, comparator_3_eq);
  or or_4 (or_4_out, comparator_4_gt, comparator_4_eq);
  Multiplexer multiplexer_1 (
    .in0(shifter_2_out[0]), .in1(1'b1), .out(multiplexer_1_out[0]), .sel(or_2_out));  // open: en
  Multiplexer #(.width(4)) multiplexer_2 (
    .in0(shifter_2_out[7:4]), .in1(subtractor_2_out), .out(multiplexer_2_out), .sel(or_2_out));  // open: en
  Multiplexer multiplexer_3 (
    .in0(shifter_3_out[0]), .in1(1'b1), .out(multiplexer_3_out[0]), .sel(or_3_out));  // open: en
  Multiplexer #(.width(4)) multiplexer_4 (
    .in0(shifter_3_out[7:4]), .in1(subtractor_3_out), .out(multiplexer_4_out), .sel(or_3_out));  // open: en
  Multiplexer multiplexer_5 (.in0(shifter_4_out[0]), .in1(1'b1), .out(quot[0]), .sel(or_4_out));  // open: en
  Multiplexer #(.width(4)) multiplexer_6 (
    .in0(shifter_4_out[7:4]), .in1(subtractor_4_out), .out(rem), .sel(or_4_out));  // open: en
  Multiplexer multiplexer_7 (
    .in0(shifter_1_out[0]), .in1(1'b1), .out(multiplexer_7_out[0]), .sel(or_1_out));  // open: en
  Multiplexer #(.width(4)) multiplexer_8 (
    .in0(shifter_1_out[7:4]), .in1(subtractor_1_out), .out(multiplexer_7_out[7:4]), .sel(or_1_out));  // open: en

  // Notes on the sheet:
  //   n1
  //   n2
  //   n1
  //   n2
  //   n1
  //   n2
  //   n1
  //   n2
  //   n1
  //   n2
endmodule

module \四位除法器测试电路  (
  input  [3:0] in_1,
  input  [3:0] in_2,
  input  [3:0] in_3,
  input  [3:0] in_4,
  output [3:0] out_5,
  output [3:0] out_6,
  output [3:0] out_7,
  output [3:0] out_8
);

  \四位除法器  \u_四位除法器_1  (.n2(in_1), .d(in_2), .quot(out_5), .rem(out_6));
  Divider #(.width(4)) divider_1 (.a(in_3), .b(in_4), .out(out_7), .rem(out_8));  // open: upper
endmodule

module \_32位除法器  (
  input  [31:0] n2,
  input  [31:0] d,
  output [31:0] quot,
  output [31:0] rem
);

  wire [31:0] div1_1_quote, div1_1_rem, div1_2_quote, div1_2_rem, div1_3_quote, div1_3_rem, div1_4_quote,
       div1_4_rem, div1_5_quote, div1_5_rem, div1_6_quote, div1_6_rem, div1_7_quote, div1_7_rem,
       div1_8_quote, div1_8_rem, div1_9_quote, div1_9_rem, div1_10_quote, div1_10_rem, div1_11_quote,
       div1_11_rem, div1_12_quote, div1_12_rem, div1_13_quote, div1_13_rem, div1_14_quote, div1_14_rem,
       div1_15_quote, div1_15_rem, div1_16_quote, div1_16_rem, div1_17_quote, div1_17_rem, div1_18_quote,
       div1_18_rem, div1_19_quote, div1_19_rem, div1_20_quote, div1_20_rem, div1_21_quote, div1_21_rem,
       div1_22_quote, div1_22_rem, div1_23_quote, div1_23_rem, div1_24_quote, div1_24_rem, div1_25_quote,
       div1_25_rem, div1_26_quote, div1_26_rem, div1_27_quote, div1_27_rem, div1_28_quote, div1_28_rem,
       div1_29_quote, div1_29_rem, div1_30_quote, div1_30_rem, div1_31_quote, div1_31_rem;

  Div1 div1_1 (.n2(n2), .d(d), .quote(div1_1_quote), .rem(div1_1_rem), .n1({32{1'b0}}));
  Div1 div1_2 (.n2(div1_25_quote), .d(d), .quote(div1_2_quote), .rem(div1_2_rem), .n1(div1_25_rem));
  Div1 div1_3 (.n2(div1_26_quote), .d(d), .quote(div1_3_quote), .rem(div1_3_rem), .n1(div1_26_rem));
  Div1 div1_4 (.n2(div1_27_quote), .d(d), .quote(div1_4_quote), .rem(div1_4_rem), .n1(div1_27_rem));
  Div1 div1_5 (.n2(div1_28_quote), .d(d), .quote(div1_5_quote), .rem(div1_5_rem), .n1(div1_28_rem));
  Div1 div1_6 (.n2(div1_29_quote), .d(d), .quote(div1_6_quote), .rem(div1_6_rem), .n1(div1_29_rem));
  Div1 div1_7 (.n2(div1_30_quote), .d(d), .quote(div1_7_quote), .rem(div1_7_rem), .n1(div1_30_rem));
  Div1 div1_8 (.n2(div1_31_quote), .d(d), .quote(div1_8_quote), .rem(div1_8_rem), .n1(div1_31_rem));
  Div1 div1_9 (.n2(div1_1_quote), .d(d), .quote(div1_9_quote), .rem(div1_9_rem), .n1(div1_1_rem));
  Div1 div1_10 (.n2(div1_2_quote), .d(d), .quote(div1_10_quote), .rem(div1_10_rem), .n1(div1_2_rem));
  Div1 div1_11 (.n2(div1_3_quote), .d(d), .quote(div1_11_quote), .rem(div1_11_rem), .n1(div1_3_rem));
  Div1 div1_12 (.n2(div1_4_quote), .d(d), .quote(div1_12_quote), .rem(div1_12_rem), .n1(div1_4_rem));
  Div1 div1_13 (.n2(div1_5_quote), .d(d), .quote(div1_13_quote), .rem(div1_13_rem), .n1(div1_5_rem));
  Div1 div1_14 (.n2(div1_6_quote), .d(d), .quote(div1_14_quote), .rem(div1_14_rem), .n1(div1_6_rem));
  Div1 div1_15 (.n2(div1_7_quote), .d(d), .quote(div1_15_quote), .rem(div1_15_rem), .n1(div1_7_rem));
  Div1 div1_16 (.n2(div1_8_quote), .d(d), .quote(div1_16_quote), .rem(div1_16_rem), .n1(div1_8_rem));
  Div1 div1_17 (.n2(div1_9_quote), .d(d), .quote(div1_17_quote), .rem(div1_17_rem), .n1(div1_9_rem));
  Div1 div1_18 (.n2(div1_10_quote), .d(d), .quote(div1_18_quote), .rem(div1_18_rem), .n1(div1_10_rem));
  Div1 div1_19 (.n2(div1_11_quote), .d(d), .quote(div1_19_quote), .rem(div1_19_rem), .n1(div1_11_rem));
  Div1 div1_20 (.n2(div1_12_quote), .d(d), .quote(div1_20_quote), .rem(div1_20_rem), .n1(div1_12_rem));
  Div1 div1_21 (.n2(div1_13_quote), .d(d), .quote(div1_21_quote), .rem(div1_21_rem), .n1(div1_13_rem));
  Div1 div1_22 (.n2(div1_14_quote), .d(d), .quote(div1_22_quote), .rem(div1_22_rem), .n1(div1_14_rem));
  Div1 div1_23 (.n2(div1_15_quote), .d(d), .quote(div1_23_quote), .rem(div1_23_rem), .n1(div1_15_rem));
  Div1 div1_24 (.n2(div1_16_quote), .d(d), .quote(div1_24_quote), .rem(div1_24_rem), .n1(div1_16_rem));
  Div1 div1_25 (.n2(div1_17_quote), .d(d), .quote(div1_25_quote), .rem(div1_25_rem), .n1(div1_17_rem));
  Div1 div1_26 (.n2(div1_18_quote), .d(d), .quote(div1_26_quote), .rem(div1_26_rem), .n1(div1_18_rem));
  Div1 div1_27 (.n2(div1_19_quote), .d(d), .quote(div1_27_quote), .rem(div1_27_rem), .n1(div1_19_rem));
  Div1 div1_28 (.n2(div1_20_quote), .d(d), .quote(div1_28_quote), .rem(div1_28_rem), .n1(div1_20_rem));
  Div1 div1_29 (.n2(div1_21_quote), .d(d), .quote(div1_29_quote), .rem(div1_29_rem), .n1(div1_21_rem));
  Div1 div1_30 (.n2(div1_22_quote), .d(d), .quote(div1_30_quote), .rem(div1_30_rem), .n1(div1_22_rem));
  Div1 div1_31 (.n2(div1_23_quote), .d(d), .quote(div1_31_quote), .rem(div1_31_rem), .n1(div1_23_rem));
  Div1 div1_32 (.n2(div1_24_quote), .d(d), .quote(quot), .rem(rem), .n1(div1_24_rem));
endmodule

module \_32位除法器测试电路  (
  input  [31:0] in_1,
  input  [31:0] in_2,
  input  [31:0] in_3,
  input  [31:0] in_4,
  output [31:0] out_5,
  output [31:0] out_6,
  output [31:0] out_7,
  output [31:0] out_8
);

  \_32位除法器  \u_32位除法器_1  (.n2(in_1), .d(in_2), .quot(out_5), .rem(out_6));
  Divider #(.width(32)) divider_1 (.a(in_3), .b(in_4), .out(out_7), .rem(out_8));  // open: upper
endmodule

module Div1 (
  input  [31:0] n1,
  input  [31:0] n2,
  input  [31:0] d,
  output [31:0] quote,
  output [31:0] rem
);

  wire comparator_1_eq, comparator_1_gt, or_1_out;
  wire [0:0] shifter_3_out;
  wire [31:0] adder_1_out, shifter_1_out, shifter_2_out, subtractor_1_out;

  Shifter #(.width(32)) shifter_1 (.in(n1), .\dist (5'b00001), .out(shifter_1_out));
  Shifter #(.width(32), .shift("lr")) shifter_2 (.in(n2), .\dist ({5{1'b1}}), .out(shifter_2_out));
  Adder #(.width(32)) adder_1 (.a(shifter_1_out), .b(shifter_2_out), .out(adder_1_out));  // open: cin, cout
  Shifter #(.width(32)) shifter_3 (.in(n2), .\dist (5'b00001), .out({quote[31:1], shifter_3_out[0]}));
  Subtractor #(.width(32)) subtractor_1 (.a(adder_1_out), .b(d), .out(subtractor_1_out));  // open: bin, bout
  or or_1 (or_1_out, comparator_1_gt, comparator_1_eq);
  Comparator #(.width(32), .mode("unsigned")) comparator_1 (
    .a(adder_1_out), .b(d), .gt(comparator_1_gt), .eq(comparator_1_eq));  // open: lt
  Multiplexer multiplexer_1 (.in0(shifter_3_out[0]), .in1(1'b1), .out(quote[0]), .sel(or_1_out));  // open: en
  Multiplexer #(.width(32)) multiplexer_2 (
    .in0(adder_1_out), .in1(subtractor_1_out), .out(rem), .sel(or_1_out));  // open: en

  // Notes on the sheet:
  //   n2
  //   n1
  //   n2
endmodule
